# Fritzing sketch FootSwitch (saved by Fritzing 0.8.5b)
breadboards: 1

parts:
  SW1 = 3PDT Switch - MovingTunes

nets:
  N1: SW1.1, SW1.2
  N2: SW1.4, SW1.5

custom parts:
  3PDT Switch - MovingTunes: 3PDT Switch
