# Fritzing sketch Jack (saved by Fritzing 0.8.5b)
breadboards: 1

parts:
  Jack_Output1 = Audio Jack MovingTunes [package=audio-jack-3.5mm-smd]

nets:
  N1: Jack_Output1.RIGHT_-_2, Jack_Output1.SLEEVE_-_3

custom parts:
  Audio Jack MovingTunes: 3.5mm Audio Jack Simple 3.5mm common PCB mount audio jack. SKU: PRT-08032 Adaptaciones por Esteban Iglesias
