# Fritzing sketch Capteur PCB (saved by Fritzing 0.9.1b)
circuit board: 4.19872cm x 4.97509cm
breadboards: 1

parts:
  Switch = Toggle Switch [package=THT]
  Arduino_Nano = Arduino Nano (Rev3.0)
  Battery = Battery block 9V
  XBee = XBee
  C1 = Ceramic Capacitor [package="100 mil [THT, multilayer]"]
  C2 = Ceramic Capacitor [package="100 mil [THT, multilayer]"]
  C6 = Ceramic Capacitor [package="100 mil [THT, multilayer]"]
  C7 = Ceramic Capacitor [package="100 mil [THT, multilayer]"]
  C8 = Ceramic Capacitor [package="100 mil [THT, multilayer]"]
  C9 = Ceramic Capacitor [package="100 mil [THT, multilayer]"]
  C10 = Ceramic Capacitor [package="100 mil [THT, multilayer]"]
  Captor = IMU Digital Combo Board 6DOF
  C11 = Ceramic Capacitor [package="100 mil [THT, multilayer]"]
  C13 = Ceramic Capacitor [package="100 mil [THT, multilayer]"]
  C14 = Ceramic Capacitor [package="100 mil [THT, multilayer]"]

nets (from the pcb view):
  3V3: Switch.COM, Arduino_Nano.3V3, Battery.+, XBee.VCC, Captor.3.3V, C14.1
  GND: Switch.L2, Arduino_Nano.GND, Battery.-, XBee.GND, C1.1, C2.1, C8.1, C10.1
  N1: Arduino_Nano.D1/TX, XBee.pin3, C7.0, C7.1, C11.1, C13.1
  N2: Arduino_Nano.A4, C6.1, Captor.SDA
  N3: C9.1, C10.0, Captor.GND

custom parts:
  Ceramic Capacitor: 100 nF multilayer Ceramic Capacitor
