# Fritzing sketch Pedale Schema 3103_2 (saved by Fritzing 0.9.1b)
circuit board: 14cm x 10cm
breadboards: 3

parts:
  U1 = XBee
  TFT1 = 1.8" TFT Display with uSD
  S3 = Momentary Switch [package=tactile_switch_smd]
  R21 = Resistor [tolerance=±5% resistance=10k package=THT]
  R1 = Resistor [tolerance=±5% resistance=10M package=THT]
  R2 = Resistor [tolerance=±5% resistance=10M package=THT]
  R4 = Resistor [tolerance=±5% resistance=100k package=THT]
  R3 = Resistor [tolerance=±5% resistance=1k package=THT]
  R6 = Resistor [tolerance=±5% resistance=100k package=THT]
  R9 = Resistor [tolerance=±5% resistance=4.7k package=THT]
  R7 = Resistor [tolerance=±5% resistance=50k package=THT]
  R5 = Resistor [tolerance=±5% resistance=500k package=THT]
  R12 = Resistor [tolerance=±5% resistance=100k package=THT]
  R8 = Resistor [tolerance=±5% resistance=100k package=THT]
  R10 = Resistor [tolerance=±5% resistance=4.7k package=THT]
  R11 = Resistor [tolerance=±5% resistance=100k package=THT]
  C1 = Ceramic Capacitor [capacitance=100nF package="100 mil [THT, multilayer]"]
  C2 = Ceramic Capacitor [capacitance=270pF package="100 mil [THT, multilayer]"]
  C4 = Ceramic Capacitor [capacitance=100nF package="100 mil [THT, multilayer]"]
  C5 = Ceramic Capacitor [capacitance=270pF package="100 mil [THT, multilayer]"]
  D1 = Rectifier Diode [part_number=1N4001 package="300 mil [THT]"]
  D2 = Rectifier Diode [part_number=1N4001 package="300 mil [THT]"]
  D3 = Rectifier Diode [part_number=1N4001 package="300 mil [THT]"]
  D4 = Rectifier Diode [part_number=1N4001 package="300 mil [THT]"]
  Rv1 = Trimmer Potentiometer [maximum_resistance=500kΩ package=THT]
  C6 = Electrolytic Capacitor [capacitance=1µF package="100 mil [THT, electrolytic]"]
  IC1 = Dual Op-Amp [package=dip08]
  U3 = AD654 - Low Cost Monolithic Voltage-to-Frequency Converter [part_number=AD654]
  C15 = Electrolytic Capacitor [capacitance=10µF package="100 mil [THT, electrolytic]"]
  C16 = Electrolytic Capacitor [capacitance=10µF package="100 mil [THT, electrolytic]"]
  SW4 = FootSwitch [package=os]
  R20 = Resistor [tolerance=±5% resistance=1k package=THT]
  LED1 = LED - 5mm [color="Red (633nm)" package="5 mm [THT]"]
  C13 = Ceramic Capacitor [capacitance=100nF package="100 mil [THT, multilayer]"]
  R18 = Resistor [tolerance=±5% resistance=100k package=THT]
  C14 = Electrolytic Capacitor [capacitance=1µF package="100 mil [THT, electrolytic]"]
  R17 = Resistor [tolerance=±5% resistance=100k package=THT]
  C11 = Ceramic Capacitor [capacitance=0.27nF package="100 mil [THT, multilayer]"]
  R19 = Resistor [tolerance=±5% resistance=100 package=THT]
  C12 = Ceramic Capacitor [capacitance=100nF package="100 mil [THT, multilayer]"]
  C9 = Ceramic Capacitor [capacitance=0.27µF package="100 mil [THT, multilayer]"]
  C7 = Ceramic Capacitor [capacitance=100nF package="100 mil [THT, multilayer]"]
  C8 = Ceramic Capacitor [capacitance=100nF package="100 mil [THT, multilayer]"]
  R13 = Resistor [tolerance=±20% resistance=100 package=THT]
  R14 = Resistor [tolerance=±5% resistance=100 package=THT]
  IC2 = Dual Op-Amp [package=dip08]
  R16 = Resistor [tolerance=±5% resistance=100k package=THT]
  C10 = Ceramic Capacitor [capacitance=0.27nF package="100 mil [THT, multilayer]"]
  Jack_Input = Audio Jack MovingTunes [package=audio-jack-3.5mm-smd]
  Jack_Output = Audio Jack MovingTunes [package=audio-jack-3.5mm-smd]
  CONN3 = Connecteur 8 Pins [package=1x20]  # not connected
  CONN2 = Connecteur 8 Pins [package=1x20]
  CONN4 = Connecteur 8 Pins [package=1x20]
  CONN5 = Connecteur 8 Pins [package=1x20]
  CONN6 = Connecteur 8 Pins [package=1x20]
  POT3 = TRIMPOT [package=trimpot-3mm-2]
  POT1 = TRIMPOT [package=trimpot-3mm-2]
  CONN1 = Connecteur 8 Pins [package=1x20]
  Composant1 = Arduino Due (Rev2b)  # not connected
  SPI = Electrolytic Capacitor [capacitance=1µF package="100 mil [THT, electrolytic]"]
  R15 = Resistor [tolerance=±20% resistance=100k package=THT]
  SW1 = SWITCH MOVING TUNES [package=kps-1290]
  SW2 = SWITCH MOVING TUNES [package=kps-1290]
  C3 = Electrolytic Capacitor [capacitance=4.7µF package="100 mil [THT, electrolytic]"]
  POT2 = TRIMPOT [package=trimpot-3mm-2]

nets (from the pcb view):
  N1: U1.VCC, R11.Pin_0, D1.cathode, D4.cathode, CONN6.4, POT3.1, POT1.1, POT2.1
  N2: U1.pin2, CONN2.1
  N3: U1.pin3, CONN2.2
  N4: U1.GND, TFT1.BL, R21.Pin_1, R1.Pin_1, R12.Pin_0, D2.anode, D3.anode, C6.-, U3.2p5V, C16.-, SW4.6, LED1.cathode, C9.0, IC2.B_+IN, Jack_Input.RIGHT_-_2, Jack_Input.SLEEVE_-_3, Jack_Output.RIGHT_-_2, Jack_Output.SLEEVE_-_3, CONN6.6, CONN6.7, POT3.3, POT1.3, R15.Pin_1, SW1.O, SW2.O, C3.-, POT2.3
  N5: TFT1.MISO, TFT1.GND, S3.1, IC1.A_V+, U3.10V, U3.V+, IC2.A_V+, CONN6.5
  N6: TFT1.SCK, CONN1.1
  N7: TFT1.MOSI, CONN1.2
  N8: TFT1.SDCS, CONN1.3
  N9: TFT1.D/C, SPI.-
  N10: TFT1.RST, SPI.+
  N11: S3.2, CONN1.5
  N12: S3.4, R21.Pin_0
  N13: R1.Pin_0, C1.1, SW4.1
  N14: R2.Pin_0, R3.Pin_1, C1.0
  N15: R2.Pin_1, R7.Pin_0, R12.Pin_1, R11.Pin_1, C6.+
  N16: R4.Pin_0, C2.0, Rv1.leg1, Rv1.wiper, IC1.A_-IN
  N17: R4.Pin_1, R9.Pin_0, C2.1, C4.1, IC1.A_OUT, C12.0
  N18: R3.Pin_0, IC1.A_+IN
  N19: R6.Pin_0, C4.0
  N20: R6.Pin_1, R8.Pin_0, C5.1, IC1.B_-IN
  N21: R9.Pin_1, D1.anode, D2.cathode, CONN5.1
  N22: R7.Pin_1, IC1.B_+IN
  N23: R5.Pin_0, C3.+
  N24: R5.Pin_1, Rv1.leg2
  N25: R8.Pin_1, R10.Pin_0, C5.0, IC1.B_OUT
  N26: R10.Pin_1, D3.cathode, D4.anode, CONN5.2
  N27: IC1.A_V-, U3.STROBE, C16.+, IC2.A_V-
  N28: U3.5V, C15.+
  N29: U3.COMMON, C15.-
  N30: SW4.2, Jack_Input.LEFT_-_1
  N31: SW4.3, SW4.9
  N32: SW4.5, CONN2.8
  N33: SW4.7, C14.-
  N34: SW4.8, Jack_Output.LEFT_-_1
  N35: R20.Pin_0, CONN2.4
  N36: R20.Pin_1, LED1.anode
  N37: C13.0, R18.Pin_0
  N38: C13.1, IC2.A_OUT, R16.Pin_1, C10.0
  N39: R18.Pin_1, R17.Pin_0, C11.1, R19.Pin_0, IC2.B_-IN
  N40: C14.+, R17.Pin_1, C11.0, IC2.B_OUT
  N41: R19.Pin_1, C12.1, SW2.P
  N42: C9.1, R14.Pin_1, IC2.A_+IN, R15.Pin_0
  N43: C7.0, R13.Pin_0
  N44: C7.1, CONN4.5
  N45: C8.0, CONN4.6
  N46: C8.1, R14.Pin_0
  N47: R13.Pin_1, IC2.A_-IN, R16.Pin_0, C10.1
  N48: CONN2.3, SW1.P
  N49: CONN5.6, POT1.2
  N50: CONN5.7, POT2.2
  N51: CONN5.8, POT3.2

notes:
  User Interface
  Output Stage

custom parts:
  1.8" TFT Display with uSD: 1.8" TFT Display with SPI control and MicroSD card
  Audio Jack MovingTunes: 3.5mm Audio Jack Simple 3.5mm common PCB mount audio jack. SKU: PRT-08032 Adaptaciones por Esteban Iglesias
  TRIMPOT: http://www.stquentin-radio.com/images/im_mag/potentiometre/pdf/C520.pdf
  SWITCH MOVING TUNES: Side-actuated SPDT slide switch, as used on the Arduino Pro
