# Fritzing sketch ShieldRecepteur (saved by Fritzing 0.9.1b)
circuit board: 5.43998cm x 8.42257cm
breadboards: 1

parts:
  Nano1 = Arduino Nano v2.3
  U3 = Potentiometre Digital [package=dip]
  R2 = Resistor [tolerance=±5% resistance=4.7k package=THT]
  U4 = Potentiometre Digital [package=dip]
  U5 = XBee
  Composants1 = Arduino Due (Rev2b)  # not connected
  Connecteur_Mesures = Connecteur 8 Pins 2 [package=1x20]
  U2 = Potentiometre Digital [package=dip]
  Connecteur_GND = Connecteur 8 Pins 2 [package=1x20]
  Connecteur_Meca2 = Connecteur 8 Pins 2 [package=1x20]  # not connected
  Connecteur_Meca1 = Connecteur 8 Pins 2 [package=1x20]  # not connected

nets:
  N1: Nano1.D1TX, U5.pin3
  N2: Nano1.D0RX, U5.pin2
  GND: Nano1.GND, U3.4_VSS, U3.7_P0B, U4.4_VSS, U4.7_P0B, U5.GND, U2.4_VSS, U2.7_P0B, Connecteur_GND.6, Connecteur_GND.7
  N3: Nano1.D10, U3.1_-_CS, U4.1_-_CS, U2.1_-_CS
  N4: Nano1.D11, R2.Pin_1
  N5: Nano1.D12, U3.3_SDI/SDO, R2.Pin_0, U4.3_SDI/SDO, U2.3_SDI/SDO
  N6: Nano1.D13, U3.2_-_SCK, U4.2_-_SCK, U2.2_-_SCK
  3V3: Nano1.3V3, U3.5_P0A, U3.8_VDD, U4.5_P0A, U4.8_VDD, U5.VCC, U2.5_P0A, U2.8_VDD
  5V: Nano1.+5V
  Mesure_2: U3.6_P0W, Connecteur_Mesures.4
  Mesure_3: U4.6_P0W, Connecteur_Mesures.5
  Mesure_1: Connecteur_Mesures.3, U2.6_P0W

custom parts:
  Connecteur 8 Pins 2: Connecteur 8 Pins
